# Fritzing sketch sketch (saved by Fritzing 0.9.3b)
perfboards: 2

parts:
  WeMos_D1_Mini1 = WeMos D1 Mini
  LED1 = LED - 5mm [color="Green (555nm)" package="5 mm [THT]"]
  LED2 = LED - 5mm [color="Red (633nm)" package="5 mm [THT]"]
  LED3 = LED - 5mm [color="Blue (430nm)" package="5 mm [THT]"]
  LED4 = LED - 5mm [color="Yellow (595nm)" package="5 mm [THT]"]
  R1 = Resistor [tolerance=±5% resistance=166k package=THT]
  R2 = Resistor [tolerance=±5% resistance=166k package=THT]
  R3 = Resistor [tolerance=±5% resistance=166k package=THT]
  R4 = Resistor [tolerance=±5% resistance=166k package=THT]

nets:
  N1: WeMos_D1_Mini1.D0, R2.Pin_1
  N2: WeMos_D1_Mini1.D3, R4.Pin_1
  N3: LED1.anode, R1.Pin_0
  N4: LED2.anode, R2.Pin_0
  N5: LED3.anode, R3.Pin_0
  N6: LED4.anode, R4.Pin_0

notes:
  GND
  EN
  VDDIN
  VIN
  BUSY
  MISO
  MOSI
  CS
  SCK
  TCM2-P102 Controller
